// Digital circuit clase.dig as structural Verilog
module clase (
  input  [3:0] A,
  input  [3:0] B,
  input  [3:0] C,
  input  [3:0] C_2,
  input  [3:0] in_6,
  input  clock,
  input  write,
  input  [2:0] Dir,
  input  enable,
  output [3:0] carry,
  output [3:0] out_7,
  output [3:0] Dout
);

  wire and_7_out, demultiplexer_1_out_0, demultiplexer_1_out_1, demultiplexer_1_out_2, demultiplexer_1_out_3,
       demultiplexer_1_out_4, demultiplexer_1_out_5, demultiplexer_1_out_6, demultiplexer_1_out_7;
  wire [3:0] and_1_out, and_2_out, and_3_out, and_4_out, and_5_out, and_6_out, multiplexer_1_out, not_1_out,
       not_2_out, not_3_out, or_2_out, register_1_q, register_2_q, register_3_q, register_4_q, register_5_q,
       register_6_q, register_7_q, register_8_q, xor_1_out, xor_2_out, xor_3_out, xor_4_out;

  assign xor_1_out = A ^ B;  // XOr xor_1, 4 bits wide
  assign xor_2_out = A ^ B;  // XOr xor_2, 4 bits wide
  assign not_1_out = ~A;  // Not not_1, 4 bits wide
  assign and_1_out = A & B;  // And and_1, 4 bits wide
  assign and_2_out = xor_1_out & C;  // And and_2, 4 bits wide
  assign and_3_out = B & not_1_out;  // And and_3, 4 bits wide
  assign xor_3_out = xor_1_out ^ C;  // XOr xor_3, 4 bits wide
  assign not_2_out = ~xor_2_out;  // Not not_2, 4 bits wide
  assign xor_4_out = in_6 ^ xor_2_out;  // XOr xor_4, 4 bits wide
  assign and_4_out = not_2_out & in_6;  // And and_4, 4 bits wide
  assign carry = and_1_out | and_2_out;  // Or or_1, 4 bits wide
  assign out_7 = and_4_out ^ and_3_out;  // XOr xor_5, 4 bits wide
  assign not_3_out = ~C_2;  // Not not_3, 4 bits wide
  assign and_5_out = xor_3_out & not_3_out;  // And and_5, 4 bits wide
  assign and_6_out = xor_4_out & C_2;  // And and_6, 4 bits wide
  assign or_2_out = and_5_out | and_6_out;  // Or or_2, 4 bits wide
  and and_7 (and_7_out, clock, write);
  Demultiplexer #(.Selector_Bits(3)) demultiplexer_1 (
    .sel(Dir), .in(1'b1), .out_0(demultiplexer_1_out_0), .out_1(demultiplexer_1_out_1),
    .out_2(demultiplexer_1_out_2), .out_3(demultiplexer_1_out_3), .out_4(demultiplexer_1_out_4),
    .out_5(demultiplexer_1_out_5), .out_6(demultiplexer_1_out_6), .out_7(demultiplexer_1_out_7));
  Register #(.Bits(4)) register_1 (.D(or_2_out), .C(and_7_out), .en(demultiplexer_1_out_0), .Q(register_1_q));
  Register #(.Bits(4)) register_2 (.D(or_2_out), .C(and_7_out), .en(demultiplexer_1_out_1), .Q(register_2_q));
  Register #(.Bits(4)) register_3 (.D(or_2_out), .C(and_7_out), .en(demultiplexer_1_out_2), .Q(register_3_q));
  Register #(.Bits(4)) register_4 (.D(or_2_out), .C(and_7_out), .en(demultiplexer_1_out_3), .Q(register_4_q));
  Register #(.Bits(4)) register_5 (.D(or_2_out), .C(and_7_out), .en(demultiplexer_1_out_4), .Q(register_5_q));
  Register #(.Bits(4)) register_6 (.D(or_2_out), .C(and_7_out), .en(demultiplexer_1_out_5), .Q(register_6_q));
  Register #(.Bits(4)) register_7 (.D(or_2_out), .C(and_7_out), .en(demultiplexer_1_out_6), .Q(register_7_q));
  Register #(.Bits(4)) register_8 (.D(or_2_out), .C(and_7_out), .en(demultiplexer_1_out_7), .Q(register_8_q));
  Multiplexer #(.Bits(4), .Selector_Bits(3)) multiplexer_1 (
    .sel(Dir), .in_0(register_1_q), .in_1(register_2_q), .in_2(register_3_q), .in_3(register_4_q),
    .in_4(register_5_q), .in_5(register_6_q), .in_6(register_7_q), .in_7(register_8_q),
    .out(multiplexer_1_out));
  D_FF #(.Bits(4)) d_ff_1 (.D(multiplexer_1_out), .C(enable), .Q(Dout));  // open: nQ

  // Notes on the sheet:
  //   sumador 4bits
  //   restador 4 bits
  //   mux 2 a 1 de 4 bits
  //   memory
endmodule
